// Logisim project DD Assignmnet final.circ as structural Verilog: 1 circuit, main circuit main
module main (
  input  in_1,
  input  in_2,
  input  in_3,
  input  in_4,
  input  in_5,
  output out_6,
  output out_7,
  output out_8
);

  wire and_1_out, and_2_out, and_3_out, and_4_out, and_5_out, and_6_out, clock_1_out, comparator_1_eq,
       comparator_2_lt, comparator_3_lt, comparator_4_lt, comparator_5_lt, decoder_1_out0, decoder_1_out1,
       decoder_1_out2, decoder_1_out3, decoder_2_out1, not_1_out, not_2_out, or_1_out;
  wire [1:0] counter_1_q;
  wire [7:0] counter_2_q, counter_3_q, counter_4_q, counter_5_q;

  Clock clock_1 (.out(clock_1_out));
  Counter #(.width(2), .max('h3)) counter_1 (
    .load(1'b0), .count(not_1_out), .Q(counter_1_q), .clk(clock_1_out), .clr(in_3));  // open: D, carry
  not not_1 (not_1_out, comparator_1_eq);
  Comparator #(.width(2), .mode("unsigned")) comparator_1 (
    .a(counter_1_q), .b({in_2, in_1}), .eq(comparator_1_eq));  // open: gt, lt
  not not_2 (not_2_out, in_3);
  Decoder #(.select(2)) decoder_1 (
    .out0(decoder_1_out0), .out1(decoder_1_out1), .out2(decoder_1_out2), .out3(decoder_1_out3),
    .sel(counter_1_q), .en(not_2_out));
  and and_1 (and_1_out, not_1_out, or_1_out);
  and and_2 (and_2_out, not_1_out, not_2_out);
  Decoder #(.select(2)) decoder_2 (
    .out0(out_6), .out1(decoder_2_out1), .out2(out_7), .out3(out_8), .sel({in_5, in_4}), .en(and_1_out));
  or or_1 (or_1_out, decoder_1_out0, decoder_1_out1, decoder_1_out2, decoder_1_out3);
  and and_3 (and_3_out, 1'b1, out_6);
  and and_4 (and_4_out, 1'b1, decoder_2_out1);
  and and_5 (and_5_out, 1'b1, out_7);
  and and_6 (and_6_out, 1'b1, out_8);
  Counter counter_2 (.load(and_3_out), .count(and_2_out), .Q(counter_2_q), .clk(clock_1_out));  // open: D, carry, clr
  Counter counter_3 (.load(and_4_out), .count(and_2_out), .Q(counter_3_q), .clk(clock_1_out));  // open: D, carry, clr
  Counter counter_4 (.load(and_5_out), .count(and_2_out), .Q(counter_4_q), .clk(clock_1_out));  // open: D, carry, clr
  Counter counter_5 (.load(and_6_out), .count(and_2_out), .Q(counter_5_q), .clk(clock_1_out));  // open: D, carry, clr
  _7_Segment_Display u_7_segment_display_1 ();  // open: g, f, a, b, e, d, c, dp
  Comparator #(.mode("unsigned")) comparator_2 (.a(counter_2_q), .b(8'hf8), .lt(comparator_2_lt));  // open: gt, eq
  LED led_1 (.in(comparator_2_lt));
  Comparator #(.mode("unsigned")) comparator_3 (.a(counter_3_q), .b(8'hf8), .lt(comparator_3_lt));  // open: gt, eq
  Comparator #(.mode("unsigned")) comparator_4 (.a(counter_4_q), .b(8'hf8), .lt(comparator_4_lt));  // open: gt, eq
  Comparator #(.mode("unsigned")) comparator_5 (.a(counter_5_q), .b(8'hf8), .lt(comparator_5_lt));  // open: gt, eq
  LED led_2 (.in(comparator_3_lt));
  LED led_3 (.in(comparator_4_lt));
  LED led_4 (.in(comparator_5_lt));
endmodule
