// Logisim project DD Assignmnet new.circ as structural Verilog: 1 circuit, main circuit main
module main (
  input  in_1,
  input  in_2,
  input  in_3,
  input  in_4,
  input  in_5,
  input  in_6,
  input  in_7,
  input  in_8,
  input  in_9,
  input  in_10,
  input  in_11,
  input  in_12,
  input  in_13,
  input  in_14,
  input  in_15,
  output out_16,
  output out_17,
  output out_18,
  output out_19,
  output out_20,
  output out_21,
  output out_22,
  output out_23
);

  wire and_1_out, clock_1_out, comparator_1_eq, comparator_2_gt, comparator_3_gt, comparator_4_gt,
       comparator_5_gt, comparator_6_gt, comparator_7_gt, comparator_8_gt, comparator_9_gt, d_ff_1_q,
       decoder_1_out0, decoder_1_out1, decoder_1_out2, decoder_1_out3, decoder_1_out4, decoder_1_out5,
       decoder_1_out6, decoder_1_out7, decoder_2_out0, decoder_2_out1, decoder_2_out2, decoder_2_out3,
       decoder_2_out4, decoder_2_out5, decoder_2_out6, decoder_2_out7, not_1_out, not_2_out, or_1_out;
  wire [2:0] counter_1_q;
  wire [7:0] counter_2_q, counter_3_q, counter_4_q, counter_5_q, counter_6_q, counter_7_q, counter_8_q,
       counter_9_q;

  Clock clock_1 (.out(clock_1_out));
  Counter #(.width(3), .max('h7)) counter_1 (
    .load(1'b0), .count(not_1_out), .Q(counter_1_q), .clk(clock_1_out), .clr(in_7));  // open: D, carry
  not not_1 (not_1_out, comparator_1_eq);
  Comparator #(.width(3), .mode("unsigned")) comparator_1 (
    .a(counter_1_q), .b({in_6, in_5, in_3}), .eq(comparator_1_eq));  // open: gt, lt
  Decoder #(.select(3)) decoder_1 (
    .out0(decoder_1_out0), .out1(decoder_1_out1), .out2(decoder_1_out2), .out3(decoder_1_out3),
    .out4(decoder_1_out4), .out5(decoder_1_out5), .out6(decoder_1_out6), .out7(decoder_1_out7),
    .sel(counter_1_q), .en(not_2_out));
  not not_2 (not_2_out, in_7);
  and and_1 (and_1_out, not_1_out, or_1_out);
  Decoder #(.select(3)) decoder_2 (
    .out0(decoder_2_out0), .out1(decoder_2_out1), .out2(decoder_2_out2), .out3(decoder_2_out3),
    .out4(decoder_2_out4), .out5(decoder_2_out5), .out6(decoder_2_out6), .out7(decoder_2_out7),
    .sel({in_14, in_13, in_11}), .en(d_ff_1_q));
  D_Flip_Flop d_ff_1 (.clk(clock_1_out), .D(and_1_out), .Q(d_ff_1_q));  // open: Qn, preset, en, reset
  or or_1 (or_1_out, decoder_1_out0, decoder_1_out1, decoder_1_out2, decoder_1_out3, decoder_1_out4, decoder_1_out5, decoder_1_out6, decoder_1_out7);
  and and_2 (out_16, d_ff_1_q, decoder_2_out0);
  and and_3 (out_17, d_ff_1_q, decoder_2_out1);
  and and_4 (out_18, d_ff_1_q, decoder_2_out2);
  and and_5 (out_19, d_ff_1_q, decoder_2_out3);
  and and_6 (out_20, d_ff_1_q, decoder_2_out4);
  and and_7 (out_21, d_ff_1_q, decoder_2_out5);
  and and_8 (out_22, d_ff_1_q, decoder_2_out6);
  and and_9 (out_23, d_ff_1_q, decoder_2_out7);
  Counter counter_2 (.count(out_16), .Q(counter_2_q), .clk(clock_1_out), .clr(in_1));  // open: load, D, carry
  Counter counter_3 (.count(out_17), .Q(counter_3_q), .clk(clock_1_out), .clr(in_2));  // open: load, D, carry
  Counter counter_4 (.count(out_18), .Q(counter_4_q), .clk(clock_1_out), .clr(in_4));  // open: load, D, carry
  Counter counter_5 (.count(out_19), .Q(counter_5_q), .clk(clock_1_out), .clr(in_8));  // open: load, D, carry
  Counter counter_6 (.count(out_20), .Q(counter_6_q), .clk(clock_1_out), .clr(in_9));  // open: load, D, carry
  Counter counter_7 (.count(out_21), .Q(counter_7_q), .clk(clock_1_out), .clr(in_10));  // open: load, D, carry
  Counter counter_8 (.count(out_22), .Q(counter_8_q), .clk(clock_1_out), .clr(in_12));  // open: load, D, carry
  Counter counter_9 (.count(out_23), .Q(counter_9_q), .clk(clock_1_out), .clr(in_15));  // open: load, D, carry
  Comparator #(.mode("unsigned")) comparator_2 (.a(counter_2_q), .b(8'hfd), .gt(comparator_2_gt));  // open: eq, lt
  LED led_1 (.in(comparator_2_gt));
  Comparator #(.mode("unsigned")) comparator_3 (.a(counter_3_q), .b(8'hfd), .gt(comparator_3_gt));  // open: eq, lt
  Comparator #(.mode("unsigned")) comparator_4 (.a(counter_4_q), .b(8'hfd), .gt(comparator_4_gt));  // open: eq, lt
  Comparator #(.mode("unsigned")) comparator_5 (.a(counter_5_q), .b(8'hfd), .gt(comparator_5_gt));  // open: eq, lt
  Comparator #(.mode("unsigned")) comparator_6 (.a(counter_6_q), .b(8'hfd), .gt(comparator_6_gt));  // open: eq, lt
  Comparator #(.mode("unsigned")) comparator_7 (.a(counter_7_q), .b(8'hfd), .gt(comparator_7_gt));  // open: eq, lt
  Comparator #(.mode("unsigned")) comparator_8 (.a(counter_8_q), .b(8'hfd), .gt(comparator_8_gt));  // open: eq, lt
  Comparator #(.mode("unsigned")) comparator_9 (.a(counter_9_q), .b(8'hfd), .gt(comparator_9_gt));  // open: eq, lt
  LED led_2 (.in(comparator_3_gt));
  LED led_3 (.in(comparator_4_gt));
  LED led_4 (.in(comparator_5_gt));
  LED led_5 (.in(comparator_6_gt));
  LED led_6 (.in(comparator_7_gt));
  LED led_7 (.in(comparator_8_gt));
  LED led_8 (.in(comparator_9_gt));
endmodule
