// Logisim project DD Assignmnet.circ as structural Verilog: 1 circuit, main circuit main
module main (
  input  in_1,
  input  in_2,
  input  in_3,
  input  in_4,
  output out_5,
  output out_6,
  output out_7,
  output out_8
);

  wire buffer_1_out, clock_1_out, comparator_1_eq, comparator_1_lt, comparator_2_lt, decoder_1_out0,
       decoder_1_out1, decoder_1_out2, decoder_1_out3, decoder_2_out0, decoder_2_out1, decoder_2_out2,
       decoder_2_out3, not_1_out, or_1_out, or_2_out;
  wire [1:0] counter_1_q, register_1_q, xor_1_out;
  wire [7:0] counter_2_q;

  Clock clock_1 (.out(clock_1_out));
  Register #(.width(2)) register_1 (
    .D({in_2, in_1}), .Q(register_1_q), .clk(clock_1_out), .clr(comparator_1_lt));  // open: en
  assign xor_1_out = register_1_q ^ {in_2, in_1};  // XOR_Gate xor_1, 2 bits wide
  Counter #(.width(2), .max('h3)) counter_1 (
    .load(1'b0), .count(comparator_1_lt), .Q(counter_1_q), .clk(clock_1_out), .clr(buffer_1_out));  // open: D, carry
  buf buffer_1 (buffer_1_out, decoder_1_out0);
  Comparator #(.width(2), .mode("unsigned")) comparator_1 (
    .a(counter_1_q), .b({in_2, in_1}), .eq(comparator_1_eq), .lt(comparator_1_lt));  // open: gt
  or or_1 (or_1_out, xor_1_out[0], xor_1_out[1]);
  Decoder #(.select(2)) decoder_1 (
    .out0(decoder_1_out0), .out1(decoder_1_out1), .out2(decoder_1_out2), .out3(decoder_1_out3),
    .sel(counter_1_q), .en(1'b1));
  Decoder #(.select(2)) decoder_2 (
    .out0(decoder_2_out0), .out1(decoder_2_out1), .out2(decoder_2_out2), .out3(decoder_2_out3),
    .sel({in_4, in_3}), .en(or_2_out));
  or or_2 (or_2_out, decoder_1_out1, decoder_1_out2, decoder_1_out3);
  not not_1 (not_1_out, comparator_1_eq);
  Counter #(.max('hf)) counter_2 (
    .load(1'b1), .D({8{1'b1}}), .count(not_1_out), .Q(counter_2_q), .clk(clock_1_out));  // open: carry, clr
  Comparator #(.mode("unsigned")) comparator_2 (.a(counter_2_q), .b(8'h7), .lt(comparator_2_lt));  // open: gt, eq
  LED led_1 (.in(comparator_2_lt));
  and and_1 (out_5, not_1_out, decoder_2_out0);
  and and_2 (out_6, not_1_out, decoder_2_out1);
  and and_3 (out_7, decoder_2_out2, not_1_out);
  and and_4 (out_8, decoder_2_out3, not_1_out);
endmodule
