// Logisim project DD Basic Circuit.circ as structural Verilog: 1 circuit, main circuit main
module main (
  input  Enable_B,
  input  [2:0] No__of_Pills,
  input  [2:0] Type_of_Pill,
  output Pill_Type_1,
  output Pill_Type_2,
  output Pill_Type_3,
  output Pill_Type_4,
  output Pill_Type_5,
  output Pill_Type_6,
  output Pill_Type_7,
  output Pill_Type_8
);

  wire and_1_out, clock_1_out, comparator_1_eq, d_ff_1_q, decoder_1_out0, decoder_1_out1, decoder_1_out2,
       decoder_1_out3, decoder_1_out4, decoder_1_out5, decoder_1_out6, decoder_1_out7, not_1_out, not_2_out,
       or_1_out;
  wire [2:0] counter_1_q;

  Clock clock_1 (.out(clock_1_out));
  Counter #(.width(3), .max('h7)) counter_1 (
    .load(1'b0), .count(not_1_out), .Q(counter_1_q), .clk(clock_1_out), .clr(Enable_B));  // open: D, carry
  not not_1 (not_1_out, comparator_1_eq);
  Comparator #(.width(3), .mode("unsigned")) comparator_1 (
    .a(counter_1_q), .b(No__of_Pills), .eq(comparator_1_eq));  // open: gt, lt
  not not_2 (not_2_out, Enable_B);
  Decoder #(.select(3)) decoder_1 (
    .out0(decoder_1_out0), .out1(decoder_1_out1), .out2(decoder_1_out2), .out3(decoder_1_out3),
    .out4(decoder_1_out4), .out5(decoder_1_out5), .out6(decoder_1_out6), .out7(decoder_1_out7),
    .sel(counter_1_q), .en(not_2_out));
  and and_1 (and_1_out, not_1_out, or_1_out);
  Decoder #(.select(3)) decoder_2 (
    .out0(Pill_Type_1), .out1(Pill_Type_2), .out2(Pill_Type_3), .out3(Pill_Type_4), .out4(Pill_Type_5),
    .out5(Pill_Type_6), .out6(Pill_Type_7), .out7(Pill_Type_8), .sel(Type_of_Pill), .en(d_ff_1_q));
  D_Flip_Flop d_ff_1 (.clk(clock_1_out), .D(and_1_out), .Q(d_ff_1_q));  // open: Qn, preset, en, reset
  or or_1 (or_1_out, decoder_1_out0, decoder_1_out1, decoder_1_out2, decoder_1_out3, decoder_1_out4, decoder_1_out5, decoder_1_out6, decoder_1_out7);
endmodule
