// Logisim project DD_with functionalities.circ as structural Verilog: 1 circuit, main circuit main
module main (
  input  in_1,
  input  in_2,
  input  in_3,
  input  in_4,
  input  in_5,
  input  in_6,
  input  in_7,
  input  in_8,
  input  in_9,
  input  in_10,
  input  in_11,
  input  in_12,
  input  in_13,
  input  in_14,
  input  in_15,
  input  [2:0] in_16,
  input  [2:0] Patient_ID,
  input  [4:0] Password,
  input  [4:0] in_19,
  input  [2:0] in_20,
  input  [4:0] in_21,
  input  [2:0] in_22,
  input  [4:0] in_23,
  input  [2:0] in_24,
  input  [4:0] in_25,
  input  [2:0] in_26,
  input  [4:0] in_27,
  input  [2:0] Patient_ID_2,
  output out_29,
  output out_30,
  output out_31,
  output out_32,
  output out_33,
  output out_34,
  output out_35,
  output out_36
);

  wire and_1_out, and_2_out, and_3_out, and_4_out, and_5_out, and_6_out, clock_1_out, comparator_1_eq,
       comparator_2_eq, comparator_3_eq, comparator_4_eq, comparator_5_eq, comparator_6_eq, comparator_7_eq,
       comparator_8_eq, comparator_9_eq, comparator_10_eq, comparator_11_eq, comparator_15_gt,
       comparator_16_gt, comparator_17_gt, comparator_18_gt, comparator_19_gt, comparator_20_gt,
       comparator_21_gt, comparator_22_gt, d_ff_1_q, decoder_1_out0, decoder_1_out1, decoder_1_out2,
       decoder_1_out3, decoder_1_out4, decoder_1_out5, decoder_1_out6, decoder_1_out7, decoder_2_out0,
       decoder_2_out1, decoder_2_out2, decoder_2_out3, decoder_2_out4, decoder_2_out5, decoder_2_out6,
       decoder_2_out7, not_1_out, not_2_out, not_3_out, or_1_out, or_2_out;
  wire [2:0] counter_1_q;
  wire [7:0] counter_2_q, counter_3_q, counter_4_q, counter_5_q, counter_6_q, counter_7_q, counter_8_q,
       counter_9_q, multiplexer_1_out, multiplexer_2_out, multiplexer_3_out;

  Clock clock_1 (.out(clock_1_out));
  Counter #(.width(3), .max('h7)) counter_1 (
    .load(1'b0), .count(not_1_out), .Q(counter_1_q), .clk(clock_1_out), .clr(in_7));  // open: D, carry
  not not_1 (not_1_out, comparator_1_eq);
  Comparator #(.width(3), .mode("unsigned")) comparator_1 (
    .a(counter_1_q), .b({in_6, in_5, in_3}), .eq(comparator_1_eq));  // open: gt, lt
  Decoder #(.select(3)) decoder_1 (
    .out0(decoder_1_out0), .out1(decoder_1_out1), .out2(decoder_1_out2), .out3(decoder_1_out3),
    .out4(decoder_1_out4), .out5(decoder_1_out5), .out6(decoder_1_out6), .out7(decoder_1_out7),
    .sel(counter_1_q), .en(not_2_out));
  not not_2 (not_2_out, in_7);
  and and_1 (and_1_out, not_1_out, or_1_out);
  Decoder #(.select(3)) decoder_2 (
    .out0(decoder_2_out0), .out1(decoder_2_out1), .out2(decoder_2_out2), .out3(decoder_2_out3),
    .out4(decoder_2_out4), .out5(decoder_2_out5), .out6(decoder_2_out6), .out7(decoder_2_out7),
    .sel({in_14, in_12, in_11}), .en(d_ff_1_q));
  D_Flip_Flop d_ff_1 (.clk(clock_1_out), .D(and_1_out), .Q(d_ff_1_q));  // open: Qn, preset, en, reset
  Comparator #(.width(3)) comparator_2 (.a(in_16), .b(Patient_ID), .eq(comparator_2_eq));  // open: gt, lt
  Comparator #(.width(5)) comparator_3 (.a(in_19), .b(Password), .eq(comparator_3_eq));  // open: gt, lt
  Comparator #(.width(3)) comparator_4 (.a(in_20), .b(Patient_ID), .eq(comparator_4_eq));  // open: gt, lt
  Comparator #(.width(5)) comparator_5 (.a(in_21), .b(Password), .eq(comparator_5_eq));  // open: gt, lt
  Comparator #(.width(3)) comparator_6 (.a(in_22), .b(Patient_ID), .eq(comparator_6_eq));  // open: gt, lt
  Comparator #(.width(5)) comparator_7 (.a(in_23), .b(Password), .eq(comparator_7_eq));  // open: gt, lt
  Comparator #(.width(3)) comparator_8 (.a(in_24), .b(Patient_ID), .eq(comparator_8_eq));  // open: gt, lt
  Comparator #(.width(5)) comparator_9 (.a(in_25), .b(Password), .eq(comparator_9_eq));  // open: gt, lt
  Comparator #(.width(3)) comparator_10 (.a(in_26), .b(Patient_ID), .eq(comparator_10_eq));  // open: gt, lt
  Comparator #(.width(5)) comparator_11 (.a(in_27), .b(Password), .eq(comparator_11_eq));  // open: gt, lt
  or or_1 (or_1_out, decoder_1_out0, decoder_1_out1, decoder_1_out2, decoder_1_out3, decoder_1_out4, decoder_1_out5, decoder_1_out6, decoder_1_out7);
  and and_2 (and_2_out, comparator_2_eq, comparator_3_eq);
  and and_3 (and_3_out, comparator_4_eq, comparator_5_eq);
  and and_4 (and_4_out, comparator_6_eq, comparator_7_eq);
  and and_5 (and_5_out, comparator_8_eq, comparator_9_eq);
  and and_6 (and_6_out, comparator_10_eq, comparator_11_eq);
  and and_7 (out_29, d_ff_1_q, decoder_2_out0);
  and and_8 (out_30, d_ff_1_q, decoder_2_out1);
  and and_9 (out_31, d_ff_1_q, decoder_2_out2);
  and and_10 (out_32, d_ff_1_q, decoder_2_out3);
  and and_11 (out_33, d_ff_1_q, decoder_2_out4);
  and and_12 (out_34, d_ff_1_q, decoder_2_out5);
  and and_13 (out_35, d_ff_1_q, decoder_2_out6);
  and and_14 (out_36, d_ff_1_q, decoder_2_out7);
  Multiplexer #(.select(3), .width(8)) multiplexer_1 (
    .in0(8'h5), .in1(8'h5), .in2(8'h5), .in3(8'h5), .in4(8'h6), .in5(8'h6), .in6(8'h6), .in7(8'h6),
    .out(multiplexer_1_out), .sel(Patient_ID_2));  // open: en
  Multiplexer #(.select(3), .width(8)) multiplexer_2 (
    .in0(8'h7), .in1(8'h7), .in2(8'h7), .in3(8'h7), .in4(8'h8), .in5(8'h8), .in6(8'h8), .in7(8'h8),
    .out(multiplexer_2_out), .sel(Patient_ID_2));  // open: en
  Multiplexer #(.select(3), .width(8)) multiplexer_3 (
    .in0(8'h4), .in1(8'h4), .in2(8'h4), .in3(8'h4), .in4(8'h3), .in5(8'h3), .in6(8'h3), .in7(8'h3),
    .out(multiplexer_3_out), .sel(Patient_ID_2));  // open: en
  Counter counter_2 (.count(out_29), .Q(counter_2_q), .clk(clock_1_out), .clr(in_1));  // open: load, D, carry
  Counter counter_3 (.count(out_30), .Q(counter_3_q), .clk(clock_1_out), .clr(in_2));  // open: load, D, carry
  Counter counter_4 (.count(out_31), .Q(counter_4_q), .clk(clock_1_out), .clr(in_4));  // open: load, D, carry
  Counter counter_5 (.count(out_32), .Q(counter_5_q), .clk(clock_1_out), .clr(in_8));  // open: load, D, carry
  Counter counter_6 (.count(out_33), .Q(counter_6_q), .clk(clock_1_out), .clr(in_9));  // open: load, D, carry
  Counter counter_7 (.count(out_34), .Q(counter_7_q), .clk(clock_1_out), .clr(in_10));  // open: load, D, carry
  Counter counter_8 (.count(out_35), .Q(counter_8_q), .clk(clock_1_out), .clr(in_13));  // open: load, D, carry
  Counter counter_9 (.count(out_36), .Q(counter_9_q), .clk(clock_1_out), .clr(in_15));  // open: load, D, carry
  or or_2 (or_2_out, and_2_out, and_3_out, and_4_out, and_5_out, and_6_out);
  Comparator #(.mode("unsigned")) comparator_12 (.b(multiplexer_1_out));  // open: a, gt, eq, lt
  Comparator #(.mode("unsigned")) comparator_13 (.b(multiplexer_2_out));  // open: a, gt, eq, lt
  Comparator #(.mode("unsigned")) comparator_14 (.b(multiplexer_3_out));  // open: a, gt, eq, lt
  not not_3 (not_3_out, or_2_out);
  Comparator #(.mode("unsigned")) comparator_15 (.a(counter_2_q), .b(8'h5), .gt(comparator_15_gt));  // open: eq, lt
  LED led_1 (.in(comparator_15_gt));
  Comparator #(.mode("unsigned")) comparator_16 (.a(counter_3_q), .b(8'h5), .gt(comparator_16_gt));  // open: eq, lt
  Comparator #(.mode("unsigned")) comparator_17 (.a(counter_4_q), .b(8'h5), .gt(comparator_17_gt));  // open: eq, lt
  Comparator #(.mode("unsigned")) comparator_18 (.a(counter_5_q), .b(8'h5), .gt(comparator_18_gt));  // open: eq, lt
  Comparator #(.mode("unsigned")) comparator_19 (.a(counter_6_q), .b(8'h5), .gt(comparator_19_gt));  // open: eq, lt
  Comparator #(.mode("unsigned")) comparator_20 (.a(counter_7_q), .b(8'h5), .gt(comparator_20_gt));  // open: eq, lt
  Comparator #(.mode("unsigned")) comparator_21 (.a(counter_8_q), .b(8'h5), .gt(comparator_21_gt));  // open: eq, lt
  Comparator #(.mode("unsigned")) comparator_22 (.a(counter_9_q), .b(8'h5), .gt(comparator_22_gt));  // open: eq, lt
  LED led_2 (.in(comparator_16_gt));
  LED led_3 (.in(comparator_17_gt));
  LED led_4 (.in(comparator_18_gt));
  LED led_5 (.in(comparator_19_gt));
  LED led_6 (.in(comparator_20_gt));
  LED led_7 (.in(comparator_21_gt));
  LED led_8 (.in(comparator_22_gt));

  // Notes on the sheet:
  //   Enable_B
endmodule
