// Logisim project demo.circ as structural Verilog: 1 circuit, main circuit main
module main (
  input  in_1,
  input  in_2,
  input  in_3
);

  wire button_1_out, clock_1_out, comparator_1_eq, nor_1_out, nor_2_out;
  wire [2:0] counter_1_q;

  Button button_1 (.out(button_1_out));
  nor nor_1 (nor_1_out, comparator_1_eq, nor_2_out);
  nor nor_2 (nor_2_out, button_1_out, nor_1_out);
  Clock clock_1 (.out(clock_1_out));
  Counter #(.width(3), .max('h7)) counter_1 (
    .count(nor_1_out), .Q(counter_1_q), .clk(clock_1_out), .clr(comparator_1_eq));  // open: load, D, carry
  Comparator #(.width(3), .mode("unsigned")) comparator_1 (
    .a(counter_1_q), .b({in_3, in_2, in_1}), .eq(comparator_1_eq));  // open: gt, lt
endmodule
